# Fritzing sketch vib_measure (saved by Fritzing 1.0.5)
breadboards: 1

parts:
  Part1 = Arduino Uno (Rev3) - ICSP
  Part2 = InvenSense MPU6050
  Part4 = Triple Axis Accelerometer Breakout - ADXL345
  A1 = u-blox NEO-6M GPS Breakout

nets:
  N1: Part1.A4/SDA, Part2.SDA, Part4.SDA
  N2: Part1.A5/SCL, Part2.SCL, Part4.SCL
  N3: Part1.D3_PWM, A1.Pin_3
  N4: Part1.D4, A1.Pin_4
  VCC: Part1.5V, Part2.VCC, Part4.VCC, A1.Pin_1
  GND: Part1.GND, Part2.GND, Part4.GND, A1.Pin_2

notes:
  ADXL345
  MPU6050
  GPS NEO-6M
